# Fritzing sketch pcb_asserv2015 (saved by Fritzing 0.9.1b)
circuit board: 8.5cm x 5.6cm
breadboards: 1

parts:
  CD3 = MMA_ACCEL_CONNECTOR [package=1x08]
  CD2 = female pin header, 9 pins [form="♀ (female)"]
  CD1 = female pin header, 9 pins [form="♀ (female)"]
  CG3 = MMA_ACCEL_CONNECTOR [package=1x08]
  CG2 = female pin header, 9 pins [form="♀ (female)"]
  CG1 = female pin header, 9 pins [form="♀ (female)"]
  DIODE = Rectifier Diode [part_number=1N4001 package="300 mil [THT]"]
  FUSE = Inductor [package="400 mil [THT]"]
  RPow = Resistor [tolerance=±5% resistance=10k package=THT]
  GND_5V_H123 = female pin header, 8 pins [form="♀ (female)"]
  GND_5V_H123_2 = female pin header, 8 pins [form="♀ (female)"]
  5V = female pin header, 2 pins [form="♀ (female)"]
  IC1 = IC, DIP package, 8 pins [chip_label=IC]
  J3 = Screw terminal - 2 pins [package=THT]
  Teensy2 = Teensy 2.0
  220f_63v = Capacitor Polarized [package=panasonic_h13]
  LED = LED - 5mm [color="Red (633nm)" package="5 mm [THT]"]
  Gauche = female pin header, 4 pins [form="♀ (female)"]
  Droite = female pin header, 4 pins [form="♀ (female)"]
  CPT_G = IC, DIP package, 14 pins [chip_label=IC]
  CPT_D = IC, DIP package, 14 pins [chip_label=IC]

nets:
  N1: CD3.VCC, Teensy2.F5
  GND: CD3.GND, CD3.X, CD3.GS1, CD2.pin2, CD2.pin3, CD2.pin5, CD1.pin5, CG3.GND, CG3.X, CG3.GS1, CG2.pin2, CG2.pin3, CG2.pin5, CG1.pin5, DIODE.cathode, RPow.Pin_1, GND_5V_H123.pin5, GND_5V_H123_2.pin5, 5V.pin2, IC1.pin5, J3.pin1, Teensy2.GND, 220f_63v.-, LED.cathode, Gauche.pin3, Droite.pin3, CPT_G.pin3, CPT_D.pin3
  N2: CD3.Y, Teensy2.F6
  N3: CD3.Z, Teensy2.F7
  N4: CD3.GS2, CG3.GS2, RPow.Pin_0
  N5: CD3.SLP, Teensy2.B5
  N6: CD2.pin6, CD1.pin6, CG2.pin6, CG1.pin6, DIODE.anode, FUSE.pin_0, 220f_63v.+
  N7: CD2.pin7, CD1.pin7, GND_5V_H123_2.pin6
  N8: CD2.pin8, CD1.pin8, GND_5V_H123_2.pin7
  N9: CD2.pin9, CD1.pin9, GND_5V_H123_2.pin8
  N10: CD1.pin1, GND_5V_H123_2.pin1
  N11: CD1.pin2, GND_5V_H123_2.pin2
  N12: CD1.pin3, GND_5V_H123_2.pin3
  N13: CD1.pin4, GND_5V_H123_2.pin4
  N14: CG3.VCC, Teensy2.F0
  N15: CG3.Y, Teensy2.F1
  N16: CG3.Z, Teensy2.F4
  N17: CG3.SLP, Teensy2.B6
  N18: CG2.pin7, CG1.pin7, GND_5V_H123.pin6
  N19: CG2.pin8, CG1.pin8, GND_5V_H123.pin7
  N20: CG2.pin9, CG1.pin9, GND_5V_H123.pin8
  N21: CG1.pin1, GND_5V_H123.pin1
  N22: CG1.pin2, GND_5V_H123.pin2
  N23: CG1.pin3, GND_5V_H123.pin3
  N24: CG1.pin4, GND_5V_H123.pin4
  N25: FUSE.pin_1, J3.pin2
  N26: 5V.pin1, IC1.pin1, Teensy2.VCC, Gauche.pin4, Droite.pin4, CPT_G.pin14, CPT_D.pin14
  N27: IC1.pin8, CPT_G.pin2, CPT_D.pin2
  N28: Teensy2.B0, LED.anode
  N29: Teensy2.B1, CPT_G.pin5, CPT_D.pin5
  N30: Teensy2.B2, CPT_G.pin7, CPT_D.pin7
  N31: Teensy2.B3, CPT_G.pin6, CPT_D.pin6
  N32: Teensy2.C6, CPT_D.pin4
  N33: Teensy2.C7, CPT_G.pin4
  N34: Gauche.pin1, CPT_G.pin11
  N35: Gauche.pin2, CPT_G.pin12
  N36: Droite.pin1, CPT_D.pin11
  N37: Droite.pin2, CPT_D.pin12

notes:
  VK
  Sorties moteurs
  Alim
  Codeurs
  USB
  Moteur Gauche
  Moteur Droit

custom parts:
  Teensy 2.0: The Teensy is a complete USB-based microcontoller development system, in a very small footprint, capable of implementing many types of projects. All programming is done via the USB port. No special programmer is needed, only a standard "Mini-B" USB cable and a PC or Macintosh with a USB port.
